# Fritzing sketch schematics (saved by Fritzing 1.0.2b)
breadboards: 1

parts:
  Mod1 = Raspberry Pi Pico W
  Squix1 = OLED 0.96" 128x64 I2C SSD1306
  LED1 = LED - 5mm [color="Green (560nm)" current=0.030A package="5 mm [THT]"]
  LED2 = LED - 5mm [color="Red (633nm)" current=0.030A package="5 mm [THT]"]
  R1 = Resistor [tolerance=±5% power=0.25W resistance=220 package=THT]
  R2 = Resistor [tolerance=±5% power=0.25W resistance=220 package=THT]
  S1 = Pushbutton [package="[THT]"]  # not connected

nets:
  N1: Mod1.pin_3, Mod1.pin_33, Squix1.GND
  N2: Mod1.pin_4, Squix1.SCL
  N3: Mod1.pin_5, Squix1.SCA
  N4: Mod1.pin_36, Squix1.VCC
  N5: LED1.cathode, R1.Pin_0
  N6: LED2.cathode, R2.Pin_0

custom parts:
  Raspberry Pi Pico W: Raspberry Pi Pico W. Based around the RP2040 microcontroller the Pico W is a low cost microcontroller device bringing Raspberry Pi quality, cost, and easy of use to the microcontroller space. The areas marked KEEPOUT in pcb silkscreen should not have traces running through them to avoid shorts on a soldered in module!
